# Fritzing sketch EozProjectFritzing (saved by Fritzing 0.9.3b)

parts:
  RHT2 = Humidity and Temperature Sensor RHT03
  Part1 = Arduino Uno (Rev3) - ICSP

nets:
  VCC: RHT2.Vcc, Part1.5V
  N1: RHT2.Data-signal, Part1.D8
  N2: RHT2.GND_1, Part1.GND
